# Fritzing sketch IP35D (saved by Fritzing 0.9.3b)
breadboards: 1

parts:
  Composant1 = Arduino Uno (Rev3)
  RGB_SMD_LED4 = SMD RGB LED (WS2812) [package=5050]
  Composant2 = Bluetooth HC-05 Macho
  RGB_SMD_LED5 = SMD RGB LED (WS2812) [package=5050]
  RGB_SMD_LED6 = SMD RGB LED (WS2812) [package=5050]
  Composant3 = TCS3200 Color Sensor

nets:
  N1: Composant1.D12/MISO, RGB_SMD_LED4.DIn
  N2: Composant1.D13/SCK, Composant3.LED
  GND: Composant1.GND, RGB_SMD_LED4.VSS, Composant2.GND, Composant3.GND
  N3: Composant1.D0/RX, Composant2.TXD
  N4: Composant1.D1/TX, Composant2.RXD
  N5: Composant1.D2, Composant3.OUT
  N6: Composant1.D3_PWM, Composant3.S3
  N7: Composant1.D4, Composant3.S2
  N8: Composant1.D5_PWM, Composant3.S1
  N9: Composant1.D6_PWM, Composant3.S0
  VCC: Composant1.5V, RGB_SMD_LED4.VCC, Composant2.VCC, Composant3.VDD
  N10: RGB_SMD_LED4.DOut, RGB_SMD_LED5.DIn
  VDD: RGB_SMD_LED4.VDD, RGB_SMD_LED5.VCC
  N11: RGB_SMD_LED5.DOut, RGB_SMD_LED6.DIn
  VDD_2: RGB_SMD_LED5.VDD, RGB_SMD_LED6.VCC

custom parts:
  TCS3200 Color Sensor: TCS3200 Color Sensor by DF Robot
